// Logisim project mainCPU.circ as structural Verilog: 4 circuits, main circuit main
module main (
);

  wire and_1_out, and_2_out, clock_1_out, not_1_out, not_2_out, or_1_out, register_1_q, undriven;
  wire [7:0] ALU_val_e, counter_1_q, demultiplexer_1_out0, demultiplexer_1_out1, demultiplexer_1_out2,
       demultiplexer_1_out3, iCode_q, multiplexer_1_out, multiplexer_2_out, multiplexer_3_out,
       multiplexer_4_out, PC_q, rA_q, ram_1_data, rB_q, Register_File_r_out_1, Register_File_r_out_2,
       rom_1_data, valA_q, valB_q, valC_q, valE_q, valM_q;

  buf and_1 (and_1_out, or_1_out);  // AND_Gate
  // OR_Gate or_1 has open pins: out=or_1_out
  Clock clock_1 (.out(clock_1_out));
  Register #(.width(1)) register_1 (.D(and_2_out), .Q(register_1_q), .clk(clock_1_out));  // open: en, clr
  not not_1 (not_1_out, register_1_q);
  Register PC (.D(counter_1_q), .en(not_1_out), .Q(PC_q), .clk(clock_1_out), .clr(and_2_out));
  Counter counter_1 (.D(PC_q), .Q(counter_1_q), .clk(and_1_out), .clr(and_2_out));  // open: load, count, carry
  and and_2 (and_2_out, iCode_q[3], iCode_q[2], iCode_q[1], iCode_q[0]);
  ROM rom_1 (.addr(PC_q), .data(rom_1_data));  // open: sel
  Demultiplexer #(.select(2), .width(8)) demultiplexer_1 (
    .out0(demultiplexer_1_out0), .out1(demultiplexer_1_out1), .out2(demultiplexer_1_out2),
    .out3(demultiplexer_1_out3), .in(rom_1_data));  // open: sel, en
  Register iCode (.D(demultiplexer_1_out0), .Q(iCode_q), .clk(clock_1_out));  // open: en, clr
  Register rA (.D(demultiplexer_1_out1), .Q(rA_q), .clk(clock_1_out));  // open: en, clr
  Register rB (.D(demultiplexer_1_out2), .Q(rB_q), .clk(clock_1_out));  // open: en, clr
  Register valC (.D(demultiplexer_1_out3), .Q(valC_q), .clk(clock_1_out));  // open: en, clr
  Multiplexer #(.select(2), .width(8)) multiplexer_1 (
    .in0(rA_q), .in1(rB_q), .in2(valE_q), .in3(valM_q), .out(multiplexer_1_out));  // open: sel, en
  Register_File Register_File (
    .w_addr(multiplexer_1_out), .r_out_1(Register_File_r_out_1), .r_out_2(Register_File_r_out_2),
    .in_6(clock_1_out));  // open: w_data, e_2, e, r_addr_1, e_3, r_addr_1_2
  Register valA (.D(Register_File_r_out_1), .Q(valA_q), .clk(clock_1_out));  // open: en, clr
  Register valB (.D(Register_File_r_out_2), .Q(valB_q), .clk(clock_1_out));  // open: en, clr
  Multiplexer #(.width(8)) multiplexer_2 (.in0(valC_q), .in1(valA_q), .out(multiplexer_2_out));  // open: sel, en
  ALU ALU (.A(multiplexer_2_out), .B(valB_q), .val_E(ALU_val_e));  // open: ALU_fun
  Register valE (.D(ALU_val_e), .Q(valE_q), .clk(clock_1_out));  // open: en, clr
  Multiplexer #(.width(8)) multiplexer_3 (
    .in0(valE_q), .in1(valA_q), .out(multiplexer_3_out), .en(not_2_out));  // open: sel
  not not_2 (not_2_out, undriven);
  Multiplexer #(.width(8)) multiplexer_4 (
    .in0(valE_q), .in1(valA_q), .out(multiplexer_4_out), .en(undriven));  // open: sel
  RAM #(.bus("separate")) ram_1 (
    .addr(multiplexer_3_out), .din(multiplexer_4_out), .data(ram_1_data));  // open: str, sel, clk, ld, clr
  Register valM (.D(ram_1_data), .Q(valM_q), .clk(clock_1_out));  // open: en, clr

  // Notes on the sheet:
  //   contents of rom_1 (hex, n*v repeats v):
  //   0 2 1 1 0 2 2 2 0 2 3 3 0 2 4 4 0 2 4 9 0 2 3 a 0 2 2 b 0 2 1 c 0 3 1 5 0 3 2 6 0 3 3 7 0 3 4 8 0 1
  //   5 9 0 1 6 a 0 1 7 b 0 1 8 c f
endmodule

module Register_File (
  input  [7:0] w_data,
  input  [7:0] r_addr_1,
  input  e,
  input  e_2,
  input  [7:0] w_addr,
  input  in_6,
  input  e_3,
  input  [7:0] r_addr_1_2,
  output [7:0] r_out_1,
  output [7:0] r_out_2
);

  wire demultiplexer_1_out0, demultiplexer_1_out1, demultiplexer_1_out2, demultiplexer_1_out3,
       demultiplexer_1_out4, demultiplexer_1_out5, demultiplexer_1_out6, demultiplexer_1_out7,
       demultiplexer_1_out8, demultiplexer_1_out9, demultiplexer_1_out10, demultiplexer_1_out11,
       demultiplexer_1_out12, demultiplexer_1_out13, demultiplexer_1_out14, demultiplexer_1_out15,
       demultiplexer_2_out0, demultiplexer_2_out1, demultiplexer_2_out2, demultiplexer_2_out3,
       demultiplexer_2_out4, demultiplexer_2_out5, demultiplexer_2_out6, demultiplexer_2_out7,
       demultiplexer_2_out8, demultiplexer_2_out9, demultiplexer_2_out10, demultiplexer_2_out11,
       demultiplexer_2_out12, demultiplexer_2_out13, demultiplexer_2_out14, demultiplexer_2_out15,
       demultiplexer_3_out0, demultiplexer_3_out1, demultiplexer_3_out2, demultiplexer_3_out3,
       demultiplexer_3_out4, demultiplexer_3_out5, demultiplexer_3_out6, demultiplexer_3_out7,
       demultiplexer_3_out8, demultiplexer_3_out9, demultiplexer_3_out10, demultiplexer_3_out11,
       demultiplexer_3_out12, demultiplexer_3_out13, demultiplexer_3_out14, demultiplexer_3_out15;
  wire [7:0] register_1_q, register_2_q, register_3_q, register_4_q, register_5_q, register_6_q,
       register_7_q, register_8_q, register_9_q, register_10_q, register_11_q, register_12_q, register_13_q,
       register_14_q, register_15_q, register_16_q;

  Demultiplexer #(.select(4)) demultiplexer_1 (
    .out0(demultiplexer_1_out0), .out1(demultiplexer_1_out1), .out2(demultiplexer_1_out2),
    .out3(demultiplexer_1_out3), .out4(demultiplexer_1_out4), .out5(demultiplexer_1_out5),
    .out6(demultiplexer_1_out6), .out7(demultiplexer_1_out7), .out8(demultiplexer_1_out8),
    .out9(demultiplexer_1_out9), .out10(demultiplexer_1_out10), .out11(demultiplexer_1_out11),
    .out12(demultiplexer_1_out12), .out13(demultiplexer_1_out13), .out14(demultiplexer_1_out14),
    .out15(demultiplexer_1_out15), .in(1'b1), .sel(w_addr[3:0]), .en(e_2));
  Register register_1 (.D(w_data), .en(demultiplexer_1_out0), .Q(register_1_q), .clk(in_6));  // open: clr
  Register register_2 (.D(w_data), .en(demultiplexer_1_out1), .Q(register_2_q), .clk(in_6));  // open: clr
  Register register_3 (.D(w_data), .en(demultiplexer_1_out2), .Q(register_3_q), .clk(in_6));  // open: clr
  Register register_4 (.D(w_data), .en(demultiplexer_1_out3), .Q(register_4_q), .clk(in_6));  // open: clr
  Register register_5 (.D(w_data), .en(demultiplexer_1_out4), .Q(register_5_q), .clk(in_6));  // open: clr
  Register register_6 (.D(w_data), .en(demultiplexer_1_out5), .Q(register_6_q), .clk(in_6));  // open: clr
  Register register_7 (.D(w_data), .en(demultiplexer_1_out6), .Q(register_7_q), .clk(in_6));  // open: clr
  Register register_8 (.D(w_data), .en(demultiplexer_1_out7), .Q(register_8_q), .clk(in_6));  // open: clr
  Register register_9 (.D(w_data), .en(demultiplexer_1_out8), .Q(register_9_q), .clk(in_6));  // open: clr
  Register register_10 (.D(w_data), .en(demultiplexer_1_out9), .Q(register_10_q), .clk(in_6));  // open: clr
  Register register_11 (.D(w_data), .en(demultiplexer_1_out10), .Q(register_11_q), .clk(in_6));  // open: clr
  Register register_12 (.D(w_data), .en(demultiplexer_1_out11), .Q(register_12_q), .clk(in_6));  // open: clr
  Register register_13 (.D(w_data), .en(demultiplexer_1_out12), .Q(register_13_q), .clk(in_6));  // open: clr
  Register register_14 (.D(w_data), .en(demultiplexer_1_out13), .Q(register_14_q), .clk(in_6));  // open: clr
  Register register_15 (.D(w_data), .en(demultiplexer_1_out14), .Q(register_15_q), .clk(in_6));  // open: clr
  Register register_16 (.D(w_data), .en(demultiplexer_1_out15), .Q(register_16_q), .clk(in_6));  // open: clr
  assign r_out_1 = demultiplexer_2_out0 ? register_1_q : 8'bz;  // Controlled_Buffer controlled_buffer_1
  assign r_out_2 = demultiplexer_3_out0 ? register_1_q : 8'bz;  // Controlled_Buffer controlled_buffer_2
  assign r_out_1 = demultiplexer_2_out1 ? register_2_q : 8'bz;  // Controlled_Buffer controlled_buffer_3
  assign r_out_2 = demultiplexer_3_out1 ? register_2_q : 8'bz;  // Controlled_Buffer controlled_buffer_4
  assign r_out_1 = demultiplexer_2_out2 ? register_3_q : 8'bz;  // Controlled_Buffer controlled_buffer_5
  assign r_out_2 = demultiplexer_3_out2 ? register_3_q : 8'bz;  // Controlled_Buffer controlled_buffer_6
  assign r_out_1 = demultiplexer_2_out3 ? register_4_q : 8'bz;  // Controlled_Buffer controlled_buffer_7
  assign r_out_2 = demultiplexer_3_out3 ? register_4_q : 8'bz;  // Controlled_Buffer controlled_buffer_8
  assign r_out_1 = demultiplexer_2_out4 ? register_5_q : 8'bz;  // Controlled_Buffer controlled_buffer_9
  assign r_out_2 = demultiplexer_3_out4 ? register_5_q : 8'bz;  // Controlled_Buffer controlled_buffer_10
  assign r_out_1 = demultiplexer_2_out5 ? register_6_q : 8'bz;  // Controlled_Buffer controlled_buffer_11
  assign r_out_2 = demultiplexer_3_out5 ? register_6_q : 8'bz;  // Controlled_Buffer controlled_buffer_12
  assign r_out_1 = demultiplexer_2_out6 ? register_7_q : 8'bz;  // Controlled_Buffer controlled_buffer_13
  assign r_out_2 = demultiplexer_3_out6 ? register_7_q : 8'bz;  // Controlled_Buffer controlled_buffer_14
  assign r_out_1 = demultiplexer_2_out7 ? register_8_q : 8'bz;  // Controlled_Buffer controlled_buffer_15
  assign r_out_2 = demultiplexer_3_out7 ? register_8_q : 8'bz;  // Controlled_Buffer controlled_buffer_16
  assign r_out_1 = demultiplexer_2_out8 ? register_9_q : 8'bz;  // Controlled_Buffer controlled_buffer_17
  assign r_out_2 = demultiplexer_3_out8 ? register_9_q : 8'bz;  // Controlled_Buffer controlled_buffer_18
  assign r_out_1 = demultiplexer_2_out9 ? register_10_q : 8'bz;  // Controlled_Buffer controlled_buffer_19
  assign r_out_2 = demultiplexer_3_out9 ? register_10_q : 8'bz;  // Controlled_Buffer controlled_buffer_20
  assign r_out_1 = demultiplexer_2_out10 ? register_11_q : 8'bz;  // Controlled_Buffer controlled_buffer_21
  assign r_out_2 = demultiplexer_3_out10 ? register_11_q : 8'bz;  // Controlled_Buffer controlled_buffer_22
  assign r_out_1 = demultiplexer_2_out11 ? register_12_q : 8'bz;  // Controlled_Buffer controlled_buffer_23
  assign r_out_2 = demultiplexer_3_out11 ? register_12_q : 8'bz;  // Controlled_Buffer controlled_buffer_24
  assign r_out_1 = demultiplexer_2_out12 ? register_13_q : 8'bz;  // Controlled_Buffer controlled_buffer_25
  assign r_out_2 = demultiplexer_3_out12 ? register_13_q : 8'bz;  // Controlled_Buffer controlled_buffer_26
  assign r_out_1 = demultiplexer_2_out13 ? register_14_q : 8'bz;  // Controlled_Buffer controlled_buffer_27
  assign r_out_2 = demultiplexer_3_out13 ? register_14_q : 8'bz;  // Controlled_Buffer controlled_buffer_28
  assign r_out_1 = demultiplexer_2_out14 ? register_15_q : 8'bz;  // Controlled_Buffer controlled_buffer_29
  assign r_out_2 = demultiplexer_3_out14 ? register_15_q : 8'bz;  // Controlled_Buffer controlled_buffer_30
  assign r_out_1 = demultiplexer_2_out15 ? register_16_q : 8'bz;  // Controlled_Buffer controlled_buffer_31
  assign r_out_2 = demultiplexer_3_out15 ? register_16_q : 8'bz;  // Controlled_Buffer controlled_buffer_32
  Demultiplexer #(.select(4)) demultiplexer_2 (
    .out0(demultiplexer_2_out0), .out1(demultiplexer_2_out1), .out2(demultiplexer_2_out2),
    .out3(demultiplexer_2_out3), .out4(demultiplexer_2_out4), .out5(demultiplexer_2_out5),
    .out6(demultiplexer_2_out6), .out7(demultiplexer_2_out7), .out8(demultiplexer_2_out8),
    .out9(demultiplexer_2_out9), .out10(demultiplexer_2_out10), .out11(demultiplexer_2_out11),
    .out12(demultiplexer_2_out12), .out13(demultiplexer_2_out13), .out14(demultiplexer_2_out14),
    .out15(demultiplexer_2_out15), .in(1'b1), .sel(r_addr_1[3:0]), .en(e));
  Demultiplexer #(.select(4)) demultiplexer_3 (
    .out0(demultiplexer_3_out0), .out1(demultiplexer_3_out1), .out2(demultiplexer_3_out2),
    .out3(demultiplexer_3_out3), .out4(demultiplexer_3_out4), .out5(demultiplexer_3_out5),
    .out6(demultiplexer_3_out6), .out7(demultiplexer_3_out7), .out8(demultiplexer_3_out8),
    .out9(demultiplexer_3_out9), .out10(demultiplexer_3_out10), .out11(demultiplexer_3_out11),
    .out12(demultiplexer_3_out12), .out13(demultiplexer_3_out13), .out14(demultiplexer_3_out14),
    .out15(demultiplexer_3_out15), .in(1'b1), .sel(r_addr_1_2[3:0]), .en(e_3));
  // also tied to GND on the sheet: {r_addr_1[4], r_addr_1[5], r_addr_1[6], r_addr_1[7], r_addr_1_2[4], r_addr_1_2[5], r_addr_1_2[6], r_addr_1_2[7]}
endmodule

module ALU (
  input  [7:0] A,
  input  [7:0] B,
  input  ALU_fun,
  output [7:0] val_E
);

  wire [7:0] multiplexer_1_out;

  Multiplexer #(.width(8)) multiplexer_1 (
    .in0({8{1'b0}}), .in1(A), .out(multiplexer_1_out), .en(ALU_fun));  // open: sel
  Adder adder_1 (.a(multiplexer_1_out), .b(B), .out(val_E));  // open: cin, cout
endmodule

module PC_Increment_Logic (
  input  [7:0] in_1
);

  Decoder #(.select(4)) decoder_1 (.sel(in_1[3:0]));  // open: out0, out1, out2, out3, out4, out5, out6, out7, out8, out9, out10, out11, out12, out13, out14, out15, en
endmodule
